# Fritzing sketch Button_LED (saved by Fritzing 1.0.1rc)
breadboards: 1

parts:
  元件1 = Adafruit T-Cobbler Plus [part_number="Adafruit #1989 and #2028"]
  R1 = Resistor [tolerance=±5% resistance=220 power=0.25W package=THT]
  S1 = Pushbutton [package="[THT]"]
  LED1 = LED - 5mm [color="Red (633nm)" current=0.030A package="5 mm [THT]"]

nets:
  N1: 元件1.GND, S1.Pin_1, S1.Pin_2, LED1.cathode
  N2: 元件1.GPIO18, S1.Pin_3, S1.Pin_4
  N3: 元件1.GPIO25, R1.Pin_1
  N4: R1.Pin_0, LED1.anode

custom parts:
  Adafruit T-Cobbler Plus: The Raspberry Pi has landed on the Maker World like a 40-GPIO pinned, quad-USB ported, credit card sized bomb of DIY joy. And while you can use most of our great Model B accessories by hooking up our downgrade cable, its probably a good time to upgrade your set up and accessorize using all of the 40 pins. That's why we now carry the Assembled Adafruit Pi T-Cobbler Plus - Breakout + Cable for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
