# Fritzing sketch pico_W基本線路圖 (saved by Fritzing 1.0.1rc)
breadboards: 1

parts:
  Mod2 = Raspberry Pi Pico W
  R1 = Resistor [tolerance=±5% power=0.25W resistance=1k package=THT]
  LED1 = LED - 5mm [color="Red (633nm)" current=0.030A package="5 mm [THT]"]
  R2 = Photocell (LDR) [power=0.25W dark_resistance_@0.01lx=300kΩ light_resistance_@100lx=400Ω luminance=10lx package=THT]
  R3 = Resistor [tolerance=±5% power=0.25W resistance=1k package=THT]
  RE1 = Rotary Encoder [package=THT]

nets:
  N1: Mod2.pin_3, Mod2.pin_8, Mod2.pin_13, Mod2.pin_18, Mod2.pin_23, Mod2.pin_28, Mod2.pin_33, Mod2.pin_38, LED1.cathode, R3.Pin_1, RE1.EncoderPinA
  N2: Mod2.pin_20, R1.Pin_0
  N3: Mod2.pin_32, RE1.EncoderPinC
  N4: Mod2.pin_34, R2.pin_0, R3.Pin_0
  N5: Mod2.pin_36, R2.pin_1, RE1.EncoderPinB
  N6: R1.Pin_1, LED1.anode

notes:
  GP28光敏電阻
  GP15,LEDTO
  GP27, 可變電阻

custom parts:
  Raspberry Pi Pico W: Raspberry Pi Pico W. Based around the RP2040 microcontroller the Pico W is a low cost microcontroller device bringing Raspberry Pi quality, cost, and easy of use to the microcontroller space. The areas marked KEEPOUT in pcb silkscreen should not have traces running through them to avoid shorts on a soldered in module!
