# Fritzing sketch button (saved by Fritzing 0.9.4)
breadboards: 1

parts:
  Εξάρτημα1 = Arduino Nano (Rev3.0)
  S1 = Pushbutton [package="[THT]"]
  LED1 = LED - 5mm [color="Red (633nm)" package="5 mm [THT]"]
  R1 = Resistor [tolerance=±5% resistance=10k package=THT]

nets:
  N1: Εξάρτημα1.GND, LED1.cathode, R1.Pin_0
  N2: Εξάρτημα1.D2, S1.Pin_3, S1.Pin_4, R1.Pin_1
  N3: Εξάρτημα1.3V3, S1.Pin_1, S1.Pin_2
  N4: Εξάρτημα1.D13/SCK, LED1.anode
