# Fritzing sketch 光敏電阻 (saved by Fritzing 0.9.4)
breadboards: 1

parts:
  Εξάρτημα1 = Arduino Nano (Rev3.0)
  LED1 = LED - 5mm [color="Red (633nm)" package="5 mm [THT]"]
  R1 = Resistor [tolerance=±5% resistance=10k package=THT]
  R2 = Photocell (LDR) [package=THT]

nets:
  N1: Εξάρτημα1.GND, LED1.cathode, R2.pin_1
  N2: Εξάρτημα1.A0, R1.Pin_1, R2.pin_0
  N3: Εξάρτημα1.3V3, R1.Pin_0
  N4: Εξάρτημα1.D13/SCK, LED1.anode
