# Fritzing sketch rgbLed (saved by Fritzing 0.9.4)
breadboards: 1

parts:
  Εξάρτημα1 = Arduino Nano (Rev3.0)
  LED1 = RGB LED (com. anode, rbg) [package="5 mm [THT]"]
  R1 = Resistor [tolerance=±5% resistance=220 package=THT]
  R2 = Resistor [tolerance=±5% resistance=220 package=THT]
  R3 = Resistor [tolerance=±5% resistance=220 package=THT]
  R4 = Rotary Potentiometer (Small) [maximum_resistance=100kΩ package=THT]
  R5 = Rotary Potentiometer (Small) [maximum_resistance=100kΩ package=THT]
  R6 = Rotary Potentiometer (Small) [maximum_resistance=100kΩ package=THT]

nets:
  N1: Εξάρτημα1.GND, LED1.common_anode, R4.leg2, R5.leg2, R6.leg2
  N2: Εξάρτημα1.D2, R2.Pin_0
  N3: Εξάρτημα1.D3, R1.Pin_0
  N4: Εξάρτημα1.D5, R3.Pin_0
  N5: Εξάρτημα1.A2, R6.wiper
  N6: Εξάρτημα1.A1, R5.wiper
  N7: Εξάρτημα1.A0, R4.wiper
  N8: Εξάρτημα1.3V3, R4.leg1, R5.leg1, R6.leg1
  N9: LED1.red_cathode, R2.Pin_1
  N10: LED1.blue_cathode, R1.Pin_1
  N11: LED1.green_cathode, R3.Pin_1
