# Fritzing sketch bitLed (saved by Fritzing 0.9.3b)
breadboards: 1

parts:
  Εξάρτημα1 = Arduino Nano (Rev3.0)
  LED1 = LED - 5mm [color="White (4500K)" package="5 mm [THT]"]
  LED2 = LED - 5mm [color="White (4500K)" package="5 mm [THT]"]
  LED3 = LED - 5mm [color="White (4500K)" package="5 mm [THT]"]
  LED4 = LED - 5mm [color="White (4500K)" package="5 mm [THT]"]
  LED5 = LED - 5mm [color="White (4500K)" package="5 mm [THT]"]
  LED6 = LED - 5mm [color="White (4500K)" package="5 mm [THT]"]
  LED7 = LED - 5mm [color="White (4500K)" package="5 mm [THT]"]
  LED8 = LED - 5mm [color="White (4500K)" package="5 mm [THT]"]

nets:
  N1: Εξάρτημα1.GND, LED1.cathode, LED2.cathode, LED3.cathode, LED4.cathode, LED5.cathode, LED6.cathode, LED7.cathode, LED8.cathode
  N2: Εξάρτημα1.D3, LED1.anode
  N3: Εξάρτημα1.D4, LED2.anode
  N4: Εξάρτημα1.D5, LED3.anode
  N5: Εξάρτημα1.D6, LED4.anode
  N6: Εξάρτημα1.D7, LED5.anode
  N7: Εξάρτημα1.D8, LED6.anode
  N8: Εξάρτημα1.D9, LED7.anode
  N9: Εξάρτημα1.D10, LED8.anode

notes:
  arduino nano 33 iot
  1外部裝置只可以是小於或等於3.3V
  2輸出電壓為3.3V
