# Fritzing sketch 7segBar (saved by Fritzing 0.9.4)
breadboards: 1

parts:
  Εξάρτημα1 = Arduino Nano (Rev3.0)
  DI2 = 7-Segment LED Display [package=THT]

nets:
  N1: Εξάρτημα1.GND, DI2.commAnode
  N2: Εξάρτημα1.D3, DI2.cathodeA
  N3: Εξάρτημα1.D4, DI2.cathodeB
  N4: Εξάρτημα1.D5, DI2.cathodeC
  N5: Εξάρτημα1.D6, DI2.cathodeD
  N6: Εξάρτημα1.D7, DI2.cathodeE
  N7: Εξάρτημα1.D8, DI2.cathodeF
  N8: Εξάρτημα1.D9, DI2.cathodeG

notes:
  arduino nano 33 iot
  1外部裝置只可以是小於或等於3.3V
  2輸出電壓為3.3V
