# Fritzing sketch 按鈕_LED_蜂鳴器 (saved by Fritzing 1.0.1rc)
breadboards: 1

parts:
  S1 = Pushbutton [package="[THT]"]
  Mod1 = Raspberry Pi Pico W
  J1 = Piezo Speaker
  R1 = Resistor [tolerance=±5% power=0.25W resistance=220 package=THT]
  LED1 = LED - 5mm [color="Red (633nm)" current=0.030A package="5 mm [THT]"]
  LED2 = LED - 5mm [color="Yellow (595nm)" current=0.030A package="5 mm [THT]"]
  R2 = Resistor [tolerance=±5% power=0.25W resistance=220 package=THT]
  LED3 = LED - 5mm [color="Green (555nm)" current=0.030A package="5 mm [THT]"]
  R3 = Resistor [tolerance=±5% power=0.25W resistance=220 package=THT]

nets:
  N1: S1.Pin_1, S1.Pin_2, Mod1.pin_21
  N2: S1.Pin_3, S1.Pin_4, Mod1.pin_36
  N3: Mod1.pin_3, Mod1.pin_8, Mod1.pin_13, Mod1.pin_18, Mod1.pin_23, Mod1.pin_28, Mod1.pin_33, Mod1.pin_38, J1.pin1, LED1.cathode, LED2.cathode, LED3.cathode
  N4: Mod1.pin_16, J1.pin2
  N5: Mod1.pin_17, R3.Pin_0
  N6: Mod1.pin_19, R2.Pin_0
  N7: Mod1.pin_20, R1.Pin_0
  N8: R1.Pin_1, LED1.anode
  N9: LED2.anode, R2.Pin_1
  N10: LED3.anode, R3.Pin_1

custom parts:
  Raspberry Pi Pico W: Raspberry Pi Pico W. Based around the RP2040 microcontroller the Pico W is a low cost microcontroller device bringing Raspberry Pi quality, cost, and easy of use to the microcontroller space. The areas marked KEEPOUT in pcb silkscreen should not have traces running through them to avoid shorts on a soldered in module!
