# Fritzing sketch 2_4雙軸xy搖桿組 (saved by Fritzing 1.0.1rc)
breadboards: 1

parts:
  Mod1 = Raspberry Pi Pico W
  Mod2 = KY-023 Dual Axis Joystick Module [package="Breakout board"]

nets:
  N1: Mod1.pin_3, Mod1.pin_8, Mod1.pin_13, Mod1.pin_18, Mod1.pin_23, Mod1.pin_28, Mod1.pin_33, Mod1.pin_38, Mod1.pin_42, Mod2.GND
  N2: Mod1.pin_21, Mod2.SW
  N3: Mod1.pin_31, Mod2.VRx
  N4: Mod1.pin_32, Mod2.VRy
  N5: Mod1.pin_36, Mod2.+5V

notes:
  電源接3.3v

custom parts:
  Raspberry Pi Pico W: Raspberry Pi Pico W. Based around the RP2040 microcontroller the Pico W is a low cost microcontroller device bringing Raspberry Pi quality, cost, and easy of use to the microcontroller space. The areas marked KEEPOUT in pcb silkscreen should not have traces running through them to avoid shorts on a soldered in module!
  KY-023 Dual Axis Joystick Module: KY-023 Dual-Axis Joystick Module.
