# Fritzing sketch 超音波感測器HC-SR04 (saved by Fritzing 1.0.1rc)
breadboards: 1

parts:
  Mod2 = Raspberry Pi Pico W
  HC-SR04_Sensor_2 = HC-SR04 Ultrasonic Distance Sensor

nets:
  N1: Mod2.pin_3, Mod2.pin_8, Mod2.pin_13, Mod2.pin_18, Mod2.pin_23, Mod2.pin_28, Mod2.pin_33, Mod2.pin_38, HC-SR04_Sensor_2.GND
  N2: Mod2.pin_21, HC-SR04_Sensor_2.TRIG
  N3: Mod2.pin_22, HC-SR04_Sensor_2.ECHO
  N4: Mod2.pin_40, HC-SR04_Sensor_2.VCC

notes:
  提供5V電壓
  Trig-> GPIO16
  Echo-> GPIO17

custom parts:
  Raspberry Pi Pico W: Raspberry Pi Pico W. Based around the RP2040 microcontroller the Pico W is a low cost microcontroller device bringing Raspberry Pi quality, cost, and easy of use to the microcontroller space. The areas marked KEEPOUT in pcb silkscreen should not have traces running through them to avoid shorts on a soldered in module!
