# Fritzing sketch lcm1602_DHT11 (saved by Fritzing 0.9.4)
breadboards: 1

parts:
  Εξάρτημα1 = Arduino Nano (Rev3.0)
  LCD2 = LCD screen
  LCM1602_IIC2 = LCM1602 IIC [part_number="LCM1602 IIC" chip_label="LCM1602 IIC" package="DIP (Dual Inline) [THT]"]
  DHT11_2 = DHT11 module
  J1 = Piezo Speaker
  S1 = Pushbutton [package="[THT]"]

nets:
  GND: Εξάρτημα1.GND, LCM1602_IIC2.GND, J1.pin1, S1.Pin_3, S1.Pin_4
  N1: Εξάρτημα1.D2, DHT11_2.VCC
  N2: Εξάρτημα1.D4, J1.pin2
  N3: Εξάρτημα1.D5, S1.Pin_1, S1.Pin_2
  5V: Εξάρτημα1.5V, LCM1602_IIC2.VCC
  N4: Εξάρτημα1.A5, LCM1602_IIC2.SCL
  N5: Εξάρτημα1.A4, LCM1602_IIC2.SDA
  VSS: LCD2.VSS, LCM1602_IIC2.VSS
  VDD: LCD2.VDD, LCM1602_IIC2.VDD
  N6: LCD2.V0, LCM1602_IIC2.V0
  N7: LCD2.RS, LCM1602_IIC2.RS
  N8: LCD2.R/W, LCM1602_IIC2.RW
  N9: LCD2.E, LCM1602_IIC2.E
  N10: LCD2.DB0, LCM1602_IIC2.D0
  N11: LCD2.DB1, LCM1602_IIC2.D1
  N12: LCD2.DB2, LCM1602_IIC2.D2
  N13: LCD2.DB3, LCM1602_IIC2.D3
  N14: LCD2.DB4, LCM1602_IIC2.D4
  N15: LCD2.DB5, LCM1602_IIC2.D5
  N16: LCD2.DB6, LCM1602_IIC2.D6
  N17: LCD2.DB7, LCM1602_IIC2.D7
  N18: LCD2.LED+, LCM1602_IIC2.A
  N19: LCD2.LED-, LCM1602_IIC2.K
  N20: LCM1602_IIC2.LED_A, LCM1602_IIC2.LED_B

notes:
  1.注意5v輸出和接線(LCM1602)
  2.一邊3.3V一邊5V
  3.arduino nano 33 iot(後面5V要焊接)

custom parts:
  LCM1602 IIC: I2C-Module to use a 1602 or 2004 LCD on with the wire.h libory Serial LCD Modul
  DHT11 module: DHT11 black pcb module
