# Fritzing sketch mfrc522 (saved by Fritzing 0.9.4)
breadboards: 1

parts:
  Εξάρτημα1 = Arduino Nano (Rev3.0)
  元件1 = RFID-RC522-v2
  LCD3 = LCD screen
  LCM1602_IIC3 = LCM1602 IIC [part_number="LCM1602 IIC" chip_label="LCM1602 IIC" package="DIP (Dual Inline) [THT]"]

nets:
  GND: Εξάρτημα1.GND, 元件1.GND, LCM1602_IIC3.GND
  N1: Εξάρτημα1.D9, 元件1.RST
  N2: Εξάρτημα1.D10, 元件1.SDA
  N3: Εξάρτημα1.D11/MOSI, 元件1.MOSI
  N4: Εξάρτημα1.D12/MISO, 元件1.MISO
  5V: Εξάρτημα1.5V, LCM1602_IIC3.VCC
  N5: Εξάρτημα1.A5, LCM1602_IIC3.SCL
  N6: Εξάρτημα1.A4, LCM1602_IIC3.SDA
  3V3: Εξάρτημα1.3V3, 元件1.3.3V
  N7: Εξάρτημα1.D13/SCK, 元件1.SCK
  VSS: LCD3.VSS, LCM1602_IIC3.VSS
  VDD: LCD3.VDD, LCM1602_IIC3.VDD
  N8: LCD3.V0, LCM1602_IIC3.V0
  N9: LCD3.RS, LCM1602_IIC3.RS
  N10: LCD3.R/W, LCM1602_IIC3.RW
  N11: LCD3.E, LCM1602_IIC3.E
  N12: LCD3.DB0, LCM1602_IIC3.D0
  N13: LCD3.DB1, LCM1602_IIC3.D1
  N14: LCD3.DB2, LCM1602_IIC3.D2
  N15: LCD3.DB3, LCM1602_IIC3.D3
  N16: LCD3.DB4, LCM1602_IIC3.D4
  N17: LCD3.DB5, LCM1602_IIC3.D5
  N18: LCD3.DB6, LCM1602_IIC3.D6
  N19: LCD3.DB7, LCM1602_IIC3.D7
  N20: LCD3.LED+, LCM1602_IIC3.A
  N21: LCD3.LED-, LCM1602_IIC3.K
  N22: LCM1602_IIC3.LED_A, LCM1602_IIC3.LED_B

notes:
  arduino nano 33 iot
  1外部裝置只可以是小於或等於3.3V
  2輸出電壓為3.3V
  RFIF-RC522pin腳
  SDA-SCK-MOSI-MISO-IRQ-GND-RST-3.3V
  SDA-可以任意pin-程式內設定
  RST-可以任意pin-程式內設定
  IRQ-可以不接

custom parts:
  RFID-RC522-v2: A simple China made RFID-RC522 Reader; do check the pin labels, as this is a MFRC522 based clone.
  LCM1602 IIC: I2C-Module to use a 1602 or 2004 LCD on with the wire.h libory Serial LCD Modul
