# Fritzing sketch led_control (saved by Fritzing 0.9.3b)
breadboards: 1

parts:
  Εξάρτημα1 = Arduino Nano (Rev3.0)
  R1 = Resistor [tolerance=±5% resistance=220 package=THT]
  LED1 = LED - 5mm [color="Red (633nm)" package="5 mm [THT]"]

nets:
  N1: Εξάρτημα1.GND, LED1.cathode
  N2: Εξάρτημα1.D13/SCK, R1.Pin_1
  N3: R1.Pin_0, LED1.anode
