# Fritzing sketch reedSwitch (saved by Fritzing 0.9.3b)
breadboards: 1

parts:
  Εξάρτημα1 = Arduino Nano (Rev3.0)
  R1 = Resistor [tolerance=±5% resistance=220 package=THT]
  LED1 = LED - 5mm [color="Red (633nm)" package="5 mm [THT]"]
  Part2 = KY-021 Mini Magnetic Reed Switch Module [package="Breakout board"]

nets:
  GND: Εξάρτημα1.GND, LED1.cathode, Part2.Vin
  N1: Εξάρτημα1.D12/MISO, Part2.S
  N2: Εξάρτημα1.3V3, Part2.-
  N3: Εξάρτημα1.D13/SCK, R1.Pin_1
  N4: R1.Pin_0, LED1.anode

custom parts:
  KY-021 Mini Magnetic Reed Switch Module: KY-021 magnetic reed switch module. A reed switch is a magnetic sensor that is normally open and gets closed when exposed to a magnetic field.
