# Fritzing sketch 上拉電阻Button (saved by Fritzing 0.9.3b)
breadboards: 1

parts:
  Εξάρτημα1 = Arduino Nano (Rev3.0)
  S1 = Pushbutton [package="[THT]"]
  LED1 = LED - 5mm [color="Red (633nm)" package="5 mm [THT]"]

nets:
  N1: Εξάρτημα1.GND, S1.Pin_3, S1.Pin_4, LED1.cathode
  N2: Εξάρτημα1.D2, S1.Pin_1, S1.Pin_2
  N3: Εξάρτημα1.D13/SCK, LED1.anode
