# Fritzing sketch ledControl (saved by Fritzing 1.0.1rc)
breadboards: 1

parts:
  Mod2 = Raspberry Pi Pico W
  R1 = Resistor [tolerance=±5% power=0.25W resistance=220 package=THT]
  LED1 = LED - 5mm [color="Red (633nm)" current=0.030A package="5 mm [THT]"]

nets:
  N1: Mod2.pin_3, Mod2.pin_8, Mod2.pin_13, Mod2.pin_18, Mod2.pin_23, Mod2.pin_28, Mod2.pin_33, Mod2.pin_38, LED1.cathode
  N2: Mod2.pin_20, R1.Pin_1
  N3: R1.Pin_0, LED1.anode

custom parts:
  Raspberry Pi Pico W: Raspberry Pi Pico W. Based around the RP2040 microcontroller the Pico W is a low cost microcontroller device bringing Raspberry Pi quality, cost, and easy of use to the microcontroller space. The areas marked KEEPOUT in pcb silkscreen should not have traces running through them to avoid shorts on a soldered in module!
