# Fritzing sketch 控制RGBLED (saved by Fritzing 0.9.4)
breadboards: 1

parts:
  Εξάρτημα1 = Arduino Nano (Rev3.0)
  LED1 = RGB LED (com. anode, rbg) [package="5 mm [THT]"]
  R1 = Resistor [tolerance=±5% resistance=220 package=THT]
  R2 = Resistor [tolerance=±5% resistance=220 package=THT]
  R3 = Resistor [tolerance=±5% resistance=220 package=THT]

nets:
  N1: Εξάρτημα1.GND, LED1.common_anode
  N2: Εξάρτημα1.D2, R2.Pin_0
  N3: Εξάρτημα1.D3, R1.Pin_0
  N4: Εξάρτημα1.D5, R3.Pin_0
  N5: LED1.red_cathode, R2.Pin_1
  N6: LED1.blue_cathode, R1.Pin_1
  N7: LED1.green_cathode, R3.Pin_1
