# Fritzing sketch SwitchButton (saved by Fritzing 0.9.4)
breadboards: 1

parts:
  Εξάρτημα1 = Arduino Nano (Rev3.0)
  DI2 = 7-Segment LED Display [package=THT]
  U1 = 74HC595 [package="DIP16 [THT]"]
  S1 = Pushbutton [package="[THT]"]

nets:
  GND: Εξάρτημα1.GND, DI2.commAnode#2, U1.GND, U1.OE, S1.Pin_3, S1.Pin_4
  N1: Εξάρτημα1.D2, U1.DS
  N2: Εξάρτημα1.D3, U1.ST_CP
  N3: Εξάρτημα1.D4, U1.SH_CP
  N4: Εξάρτημα1.D5, S1.Pin_1, S1.Pin_2
  3V3: Εξάρτημα1.3V3, U1.MR, U1.VCC
  N5: DI2.cathodeE, U1.Q5
  N6: DI2.cathodeD, U1.Q4
  N7: DI2.cathodeC, U1.Q3
  N8: DI2.cathodeB, U1.Q2
  N9: DI2.cathodeA, U1.Q1
  N10: DI2.cathodeF, U1.Q6
  N11: DI2.cathodeG, U1.Q7

notes:
  arduino nano 33 iot
  1外部裝置只可以是小於或等於3.3V
  2輸出電壓為3.3V
