# Fritzing sketch DHT11 (saved by Fritzing 0.9.4)
breadboards: 1

parts:
  Εξάρτημα1 = Arduino Nano (Rev3.0)
  DHT11_2 = DHT11 module

nets:
  N1: Εξάρτημα1.D2, DHT11_2.VCC
  N2: Εξάρτημα1.3V3, DHT11_2.DATA

notes:
  arduino nano 33 iot
  1外部裝置只可以是小於或等於3.3V
  2輸出電壓為3.3V

custom parts:
  DHT11 module: DHT11 black pcb module
