# Fritzing sketch touch_sensor (saved by Fritzing 0.9.3b)
breadboards: 1

parts:
  Εξάρτημα1 = Arduino Nano (Rev3.0)
  R1 = Resistor [tolerance=±5% resistance=220 package=THT]
  LED1 = LED - 5mm [color="Red (633nm)" package="5 mm [THT]"]
  U2 = TOUCH [package=touch2]

nets:
  N1: Εξάρτημα1.GND, LED1.cathode, U2.touch_sensor
  N2: Εξάρτημα1.D12/MISO, U2.pin_4
  N3: Εξάρτημα1.3V3, U2.T2
  N4: Εξάρτημα1.D13/SCK, R1.Pin_1
  N5: R1.Pin_0, LED1.anode

custom parts:
  TOUCH: Electrode for resistive touch detection
