# Fritzing sketch dht11 (saved by Fritzing 0.9.3b)
breadboards: 1

parts:
  Εξάρτημα1 = Arduino Nano (Rev3.0)
  Part4 = KY-015 Temperature & Humidity Sensor Module [package="Breakout board"]

nets:
  GND: Εξάρτημα1.GND, Part4.GND
  N1: Εξάρτημα1.D11/MOSI, Part4.Data
  3V3: Εξάρτημα1.3V3, Part4.VCC

notes:
  GND_DATA_VCC

custom parts:
  KY-015 Temperature & Humidity Sensor Module: KY-015 temperature and humidity sensor module, provides a low-latency serial interface to measure humidity and temperature.
