# Fritzing sketch led_touch_dht11 (saved by Fritzing 0.9.3b)
breadboards: 1

parts:
  Εξάρτημα1 = Arduino Nano (Rev3.0)
  Part4 = KY-015 Temperature & Humidity Sensor Module [package="Breakout board"]
  U3 = TOUCH [package=touch2]
  LED2 = LED - 5mm [color="Red (633nm)" package="5 mm [THT]"]
  R2 = Resistor [tolerance=±5% resistance=220 package=THT]

nets:
  GND: Εξάρτημα1.GND, Part4.GND, U3.touch_sensor, LED2.cathode
  N1: Εξάρτημα1.D11/MOSI, Part4.Data
  N2: Εξάρτημα1.D12/MISO, U3.pin_4
  3V3: Εξάρτημα1.3V3, Part4.VCC, U3.T2
  N3: Εξάρτημα1.D13/SCK, R2.Pin_1
  N4: LED2.anode, R2.Pin_0

notes:
  GND_DATA_VCC

custom parts:
  KY-015 Temperature & Humidity Sensor Module: KY-015 temperature and humidity sensor module, provides a low-latency serial interface to measure humidity and temperature.
  TOUCH: Electrode for resistive touch detection
