# Fritzing sketch 光敏電阻_led_可變電阻_溫度 (saved by Fritzing 1.0.1rc)
breadboards: 1

parts:
  Mod2 = Raspberry Pi Pico W
  R1 = Photocell (LDR) [power=0.25W dark_resistance_@0.01lx=300kΩ light_resistance_@100lx=400Ω luminance=10lx package=THT]
  R2 = Resistor [tolerance=±5% power=0.25W resistance=10k package=THT]
  R3 = Rotary Potentiometer (Small) [maximum_resistance=10kΩ knob_status=50% power=0.5W package=THT]
  R4 = Resistor [tolerance=±5% power=0.25W resistance=220 package=THT]
  LED1 = LED - 5mm [color="Red (633nm)" current=0.030A package="5 mm [THT]"]

nets:
  N1: Mod2.pin_3, Mod2.pin_8, Mod2.pin_13, Mod2.pin_18, Mod2.pin_23, Mod2.pin_28, Mod2.pin_33, Mod2.pin_38, R2.Pin_0, R3.leg2, LED1.cathode
  N2: Mod2.pin_20, R4.Pin_1
  N3: Mod2.pin_31, R3.wiper
  N4: Mod2.pin_34, R1.pin_1, R2.Pin_1
  N5: Mod2.pin_36, R1.pin_0, R3.leg1
  N6: R4.Pin_0, LED1.anode

notes:
  LED
  220歐姆
  GPIO15
  可變電阻
  GPIO 26
  光敏電阻
  10k歐姆分壓
  GPIO28

custom parts:
  Raspberry Pi Pico W: Raspberry Pi Pico W. Based around the RP2040 microcontroller the Pico W is a low cost microcontroller device bringing Raspberry Pi quality, cost, and easy of use to the microcontroller space. The areas marked KEEPOUT in pcb silkscreen should not have traces running through them to avoid shorts on a soldered in module!
